# Fritzing sketch SimplePotentiometerInput (saved by Fritzing 0.9.2b)
breadboards: 1

parts:
  Part1 = Arduino Uno (Rev3)
  R1 = Rotary Potentiometer (Small) [maximum_resistance=100kΩ package=THT]
  R2 = Rotary Potentiometer (Small) [maximum_resistance=100kΩ package=THT]
  S1 = Toggle Switch [package=THT]
  R3 = Resistor [tolerance=±20% resistance=10k package=THT]

nets:
  N1: Part1.A0, R1.wiper
  N2: Part1.A1, R2.wiper
  N3: Part1.D0/RX, S1.COM
  N4: Part1.5V, R1.leg1, R2.leg1, S1.L2
  N5: Part1.GND, R1.leg2, R2.leg2, R3.Pin_0
  N6: S1.L1, R3.Pin_1
